# Fritzing sketch circuit-2 (saved by Fritzing 0.9.6b)
breadboards: 1

parts:
  VCC1 = Battery
  R4 = Slide Potentiometer [maximum_resistance=100Ω knob_status=0.1k%]
  AM1 = Multimeter (DC Voltage)
  R5 = Resistor [tolerance=±5% power=0.25 resistance=220 package=THT]

nets:
  N1: VCC1.-, R5.Pin_0
  N2: VCC1.+, R4.wiper, AM1.COM_Probe
  N3: R4.leg1, AM1.V_Probe, R5.Pin_1
