# Fritzing sketch circuit-3 (saved by Fritzing 0.9.6b)
breadboards: 1

parts:
  VCC1 = Battery
  AM1 = Multimeter (DC Voltage)
  R1 = Resistor [tolerance=±5% power=0.25 resistance=220 package=THT]
  S2 = Pushbutton [package=THT]

nets:
  N1: VCC1.-, AM1.COM_Probe, S2.leg0
  N2: VCC1.+, R1.Pin_0
  N3: AM1.V_Probe, R1.Pin_1, S2.leg1
