# Fritzing sketch circuit-4 (saved by Fritzing 0.9.6b)
breadboards: 1

parts:
  VCC1 = Battery
  R1 = Resistor [tolerance=±5% power=0.25 resistance=21 package=THT]
  LED1 = LED - 5mm [color="Red (633nm)" current=0.030 package="5 mm [THT]"]
  M1 = fc-51 [package=THT]

nets:
  N1: VCC1.-, LED1.cathode, M1.pin2
  N2: VCC1.+, M1.pin3
  N3: R1.Pin_0, LED1.anode
  N4: R1.Pin_1, M1.pin1
