# Fritzing sketch circuit-5 (saved by Fritzing 0.9.6b)
breadboards: 1

parts:
  J1 = Infrared Proximity Sensor [distance_to_obstacle=0%]
  VM1 = Multimeter (DC Voltage)
  VCC1 = 4 x AAA Battery Mount

nets:
  N1: J1.Vout, VM1.COM_Probe
  N2: J1.GND, VM1.V_Probe, VCC1.-
  N3: J1.Vcc, VCC1.+
