# Fritzing sketch circuit-6 (saved by Fritzing 0.9.6b)
breadboards: 1

parts:
  VCC1 = 4 x AAA Battery Mount
  M1 = DC Motor [voltage_(max)=6V voltage_(min)=3V]
  S2 = Pushbutton [package=THT]
  S3 = Pushbutton [package=THT]
  S1 = Pushbutton [package=THT]
  S4 = Pushbutton [package=THT]

nets:
  N1: VCC1.-, S2.leg1, S4.leg0
  N2: VCC1.+, S3.leg0, S1.leg1
  N3: M1.pin_1, S3.leg1
  N4: M1.pin_2, S2.leg0, S1.leg0
