# Fritzing sketch test-circuit (saved by Fritzing 0.9.6b)
breadboards: 1

parts:
  VCC1 = Battery
  LED1 = LED - 5mm [color="Red (633nm)" current=0.030 package="5 mm [THT]"]
  R3 = Resistor [tolerance=±5% power=0.25 resistance=30 package=THT]
  R4 = Slide Potentiometer [maximum_resistance=50Ω knob_status=0%]

nets:
  N1: VCC1.-, R3.Pin_0
  N2: VCC1.+, LED1.anode
  N3: LED1.cathode, R4.wiper
  N4: R3.Pin_1, R4.leg1
